// Digital circuit MUX.dig as structural Verilog
module MUX (
  input  D,
  input  C,
  input  B,
  input  A,
  input  D_2,
  input  C_2,
  input  B_2,
  input  A_2,
  output Y
);

  wire not_1_out;

  Multiplexer #(.Selector_Bits(3)) multiplexer_1 (
    .sel({A_2, B_2, D_2}), .in_0(1'b0), .in_1(1'b1));  // open: in_2, in_3, in_4, in_5, in_6, in_7, out
  not not_1 (not_1_out, A);
  Multiplexer #(.Selector_Bits(3)) multiplexer_2 (
    .sel({B, C, D}), .in_0(A), .in_1(not_1_out), .in_2(A), .in_3(not_1_out), .in_4(A), .in_5(not_1_out),
    .in_6(A), .in_7(not_1_out), .out(Y));

  // Notes on the sheet:
  //   Use A as the most-significant bit and 
  //   D as the least-significant bit.
  //   Converts between single bits & a 3-bit bus
endmodule

/* Test case:
A B C D Y
0 0 0 0 X
0 0 0 1 1
*/
